# Fritzing sketch Schematic (saved by Fritzing 0.9.3b)
breadboards: 1

parts:
  R1 = Resistor [tolerance=±5% resistance=220 package=THT]
  R2 = Resistor [tolerance=±5% resistance=220 package=THT]
  R3 = Resistor [tolerance=±5% resistance=220 package=THT]
  LED1 = LED - 5mm [color="Red (633nm)" package="5 mm [THT]"]
  LED2 = LED - 5mm [color="Red (633nm)" package="5 mm [THT]"]
  LED3 = LED - 5mm [color="Red (633nm)" package="5 mm [THT]"]
  J1 = Basic Servo
  J2 = Basic Servo
  VCC1 = 4 x AAA Battery Mount
  Arduino = Arduino Uno (Rev3)
  Raspberry_Pi1 = Raspberry Pi B rev2
  R4 = Resistor [tolerance=±5% resistance=107k package=THT]
  R5 = Resistor [tolerance=±5% resistance=150k package=THT]
  VCC2 = 4 x AAA Battery Mount
  ADC = MCP3008 8-channel 10-bit ADC [part_number=MCP3008]
  R6 = Resistor [tolerance=±5% resistance=150k package=THT]
  R7 = Resistor [tolerance=±5% resistance=80.5k package=THT]

nets:
  N1: R1.Pin_0, LED1.anode
  N2: R1.Pin_1, Raspberry_Pi1.GPIO_27
  N3: R2.Pin_0, LED3.anode
  N4: R2.Pin_1, Raspberry_Pi1.GPIO_4
  N5: R3.Pin_0, LED2.anode
  N6: R3.Pin_1, Raspberry_Pi1.GPIO_22
  GND: LED1.cathode, J1.gnd, VCC1.-, Arduino.GND, Raspberry_Pi1.GND, R4.Pin_0, VCC2.-, ADC.no_name_yet#9, ADC.no_name_yet#14
  VCC: J1.vcc, J2.vcc, VCC1.+, R5.Pin_1
  N7: J1.pulse, Arduino.D9_PWM
  N8: J2.pulse, Arduino.D10_PWM/SS
  N9: Arduino.A4/SDA, Raspberry_Pi1.GPIO_2
  N10: Arduino.A5/SCL, Raspberry_Pi1.GPIO_3
  N11: Arduino.VIN, VCC2.+, R6.Pin_0
  N12: Raspberry_Pi1.3V3, ADC.no_name_yet#15, ADC.no_name_yet#16
  N13: Raspberry_Pi1.GPIO_10, ADC.no_name_yet#11
  N14: Raspberry_Pi1.GPIO_9, ADC.no_name_yet#12
  N15: Raspberry_Pi1.GPIO_11, ADC.no_name_yet#13
  N16: Raspberry_Pi1.GPIO_8, ADC.no_name_yet#10
  N17: R4.Pin_1, R5.Pin_0, ADC.no_name_yet#1
  N18: ADC.no_name_yet#2, R7.Pin_1
  N19: R6.Pin_1, R7.Pin_0
